// Logisim project 8BitCPU_Final.circ as structural Verilog: 5 circuits, main circuit Top
module Top (
  input  Enable
);

  wire alu4bit_1_cout, alu4bit_1_sign, alu4bit_1_zero_flag, and_1_out, and_2_out, and_3_out, and_4_out,
       and_5_out, and_6_out, and_7_out, and_8_out, and_9_out, and_10_out, and_11_out, and_12_out, and_13_out,
       and_14_out, and_15_out, buffer_1_out, Clock_out, controlled_buffer_1_out, d_ff_1_q, d_ff_2_q, imm_out,
       ja_out, jb_out, je_out, jmp_out, not_4_out, not_7_out, or_1_out, r__r_out, xnor_1_out, xor_1_out,
       xor_2_out, xor_3_out, xor_4_out;
  wire [0:0] not_1_out, not_2_out, not_3_out, not_8_out;
  wire [2:0] flags;
  wire [6:0] not_5_out;
  wire [7:0] A_q, alu4bit_1_output, B_q, counter_1_q, multiplexer_1_out, multiplexer_2_out,
       multiplexer_3_out, ram_1_data;
  wire [7:2] register_1_q;
  wire [11:2] undriven;
  wire [14:13] or_2_out;
  wire [17:0] controlled_buffer_2_out;

  Clock Clock (.out(Clock_out));
  D_Flip_Flop d_ff_1 (.clk(Enable), .D(Clock_out), .Q(d_ff_1_q));  // open: Qn, preset, en, reset
  // Probe on controlled_buffer_2_out
  xnor xnor_1 (xnor_1_out, d_ff_1_q, Clock_out);
  // Probe on controlled_buffer_2_out[5:4]
  // Probe on controlled_buffer_2_out[3:2]
  xor xor_1 (xor_1_out, not_5_out[4], not_5_out[2]);
  and and_1 (and_1_out, not_4_out, and_6_out);
  and and_2 (and_2_out, and_1_out, xor_1_out);
  assign controlled_buffer_1_out = and_2_out ? 1'b1 : 1'bz;  // Controlled_Buffer controlled_buffer_1
  assign controlled_buffer_2_out = and_2_out ? {13'h1a08, not_5_out[2], 2'b10, not_5_out[4], not_2_out[0]} : 18'bz;  // Controlled_Buffer controlled_buffer_2
  and and_3 (and_3_out, not_4_out, and_7_out);
  not not_1 (not_1_out[0], not_5_out[4]);
  assign controlled_buffer_1_out = and_3_out ? 1'b1 : 1'bz;  // Controlled_Buffer controlled_buffer_3
  assign controlled_buffer_2_out = and_3_out ? {2'b10, not_5_out[2], 13'h4a, not_5_out[4], not_1_out[0]} : 18'bz;  // Controlled_Buffer controlled_buffer_4
  and and_4 (and_4_out, not_4_out, and_8_out);
  assign controlled_buffer_1_out = and_4_out ? 1'b1 : 1'bz;  // Controlled_Buffer controlled_buffer_5
  assign controlled_buffer_2_out = and_4_out ? {2'b00, not_5_out[4], 10'h88, not_5_out[2], 4'b1000} : 18'bz;  // Controlled_Buffer controlled_buffer_6
  // Probe on controlled_buffer_2_out[16:15]
  not not_2 (not_2_out[0], not_5_out[4]);
  // Probe on alu4bit_1_output
  Counter counter_1 (
    .load(controlled_buffer_2_out[13]), .D(alu4bit_1_output), .count(controlled_buffer_2_out[14]),
    .Q(counter_1_q), .clk(xor_2_out), .clr(Enable));  // open: carry
  xor xor_2 (xor_2_out, xnor_1_out, buffer_1_out);
  buf buffer_1 (buffer_1_out, xnor_1_out);
  assign controlled_buffer_1_out = and_5_out ? 1'b1 : 1'bz;  // Controlled_Buffer controlled_buffer_7
  Register A (.D(alu4bit_1_output), .en(controlled_buffer_2_out[0]), .Q(A_q), .clk(xnor_1_out), .clr(Enable));
  Register B (.D(alu4bit_1_output), .en(controlled_buffer_2_out[1]), .Q(B_q), .clk(xnor_1_out), .clr(Enable));
  Multiplexer #(.select(2), .width(8)) multiplexer_1 (
    .in0(A_q), .in1(B_q), .in2(counter_1_q), .out(multiplexer_1_out), .sel(controlled_buffer_2_out[16:15]));  // open: in3, en
  // Probe on multiplexer_1_out
  // Probe on {register_1_q[7:4], not_5_out[6], register_1_q[2], not_5_out[4], not_5_out[2]}
  and and_5 (and_5_out, and_1_out, ~xor_1_out);  // AND_Gate
  not not_3 (not_3_out[0], not_5_out[4]);
  assign controlled_buffer_2_out = and_5_out ? {16'hd04a, not_5_out[4], not_3_out[0]} : 18'bz;  // Controlled_Buffer controlled_buffer_8
  // Probe on multiplexer_2_out
  // Probe on multiplexer_3_out
  Multiplexer #(.select(2), .width(8)) multiplexer_2 (
    .in0(A_q), .in1(B_q), .in2(ram_1_data), .out(multiplexer_2_out), .sel(controlled_buffer_2_out[5:4]));  // open: in3, en
  Multiplexer #(.select(2), .width(8)) multiplexer_3 (
    .in0(A_q), .in1(B_q), .in2({8{1'b0}}), .in3(ram_1_data), .out(multiplexer_3_out),
    .sel(controlled_buffer_2_out[3:2]));  // open: en
  ALU4Bit alu4bit_1 (
    .in_2(multiplexer_2_out), .in_3(multiplexer_3_out), .\output (alu4bit_1_output),
    .zero_flag(alu4bit_1_zero_flag), .Cout(alu4bit_1_cout), .Op_Select(controlled_buffer_2_out[8:6]),
    .Sign(alu4bit_1_sign));
  RAM ram_1 (
    .addr(multiplexer_1_out), .data(ram_1_data), .sel(1'b1), .clk(xnor_1_out),
    .ld(controlled_buffer_2_out[17]));  // open: clr
  and and_6 (and_6_out, ~register_1_q[7], ~register_1_q[6], ~register_1_q[5], ~register_1_q[4], ~not_5_out[6], ~register_1_q[2]);  // AND_Gate
  and and_7 (and_7_out, ~register_1_q[7], ~register_1_q[6], ~register_1_q[5], ~register_1_q[4], ~not_5_out[6], register_1_q[2]);  // AND_Gate
  and and_8 (and_8_out, ~register_1_q[7], ~register_1_q[6], ~register_1_q[5], ~register_1_q[4], not_5_out[6], ~register_1_q[2]);  // AND_Gate
  and and_9 (and_9_out, xnor_1_out, d_ff_2_q);
  assign controlled_buffer_2_out = and_9_out ? {6'b110100, undriven, 2'b00} : 18'bz;  // Controlled_Buffer controlled_buffer_9
  not not_4 (not_4_out, and_9_out);
  D_Flip_Flop d_ff_2 (
    .clk(xnor_1_out), .D(controlled_buffer_1_out), .Q(d_ff_2_q), .preset(xnor_1_out));  // open: Qn, en, reset
  D_Flip_Flop zero (
    .clk(xnor_1_out), .D(alu4bit_1_zero_flag), .Q(flags[0]), .en(controlled_buffer_2_out[9]), .reset(Enable));  // open: Qn, preset
  // Probe on ram_1_data
  Register #(.trigger("falling")) register_1 (
    .D(ram_1_data), .en(d_ff_2_q),
    .Q({register_1_q[7:4], not_5_out[6], register_1_q[2], not_5_out[4], not_5_out[2]}), .clk(xnor_1_out),
    .clr(Enable));
  // Probe on {register_1_q[7:4], not_5_out[6], register_1_q[2], not_5_out[4], not_5_out[2]}
  and and_10 (and_10_out, d_ff_2_q, ~controlled_buffer_1_out);  // AND_Gate
  // Probe on alu4bit_1_output
  D_Flip_Flop Cout (
    .clk(xnor_1_out), .D(alu4bit_1_cout), .Q(flags[1]), .en(controlled_buffer_2_out[10]), .reset(Enable));  // open: Qn, preset
  D_Flip_Flop Sign (
    .clk(xnor_1_out), .D(alu4bit_1_sign), .Q(flags[2]), .en(controlled_buffer_2_out[11]), .reset(Enable));  // open: Qn, preset
  and and_11 (and_11_out, ~register_1_q[7], ~register_1_q[6], ~register_1_q[5], register_1_q[4]);  // AND_Gate
  assign controlled_buffer_1_out = imm_out ? 1'b1 : 1'bz;  // Controlled_Buffer controlled_buffer_10
  and and_12 (and_12_out, ~register_1_q[7], ~register_1_q[6], register_1_q[5], ~register_1_q[4], ~not_5_out[6]);  // AND_Gate
  D_Flip_Flop d_ff_3 (.clk(xnor_1_out), .D(and_10_out), .reset(xnor_1_out));  // open: Q, Qn, preset, en
  assign ram_1_data = controlled_buffer_2_out[12] ? alu4bit_1_output : 8'bz;  // Controlled_Buffer controlled_buffer_11
  not not_5 (not_5_out[0], not_5_out[4]);
  and and_13 (and_13_out, not_4_out, and_11_out);
  and imm (imm_out, and_13_out, xor_4_out);
  assign controlled_buffer_2_out = imm_out ? {11'h61e, not_5_out[6], 1'b0, not_5_out[4], 1'b0, not_5_out[2], not_5_out[4], not_5_out[0]} : 18'bz;  // Controlled_Buffer controlled_buffer_12
  assign controlled_buffer_1_out = and_14_out ? 1'b1 : 1'bz;  // Controlled_Buffer controlled_buffer_13
  and je (je_out, flags[0], ~not_5_out[4], ~not_5_out[2]);  // AND_Gate
  and and_14 (and_14_out, not_4_out, and_12_out);
  or or_1 (or_1_out, je_out, ja_out, jb_out);
  xor xor_3 (xor_3_out, or_1_out, register_1_q[2]);
  not not_6 (or_2_out[14], or_2_out[13]);
  assign controlled_buffer_2_out = and_14_out ? {3'b110, or_2_out, 13'h128} : 18'bz;  // Controlled_Buffer controlled_buffer_14
  xor xor_4 (xor_4_out, not_5_out[2], not_5_out[4]);
  assign controlled_buffer_1_out = r__r_out ? 1'b1 : 1'bz;  // Controlled_Buffer controlled_buffer_15
  and and_15 (and_15_out, ~flags[0], flags[1]);  // AND_Gate
  and ja (ja_out, and_15_out, ~not_5_out[4], not_5_out[2]);  // AND_Gate
  or or_2 (or_2_out[13], xor_3_out, jmp_out);
  not not_7 (not_7_out, xor_4_out);
  not not_8 (not_8_out[0], not_5_out[2]);
  and r__r (r__r_out, and_13_out, not_7_out);
  assign controlled_buffer_2_out = r__r_out ? {11'h69e, not_5_out[6], 1'b0, not_5_out[2], 2'b11, not_5_out[2], not_8_out[0]} : 18'bz;  // Controlled_Buffer controlled_buffer_16
  and jb (jb_out, ~flags[1], not_5_out[4], ~not_5_out[2]);  // AND_Gate
  and jmp (jmp_out, ~register_1_q[2], not_5_out[4], not_5_out[2]);  // AND_Gate

  // Notes on the sheet:
  //   mov r, r
  //   reset to phase 1
  //   mov r,  [r]
  //   mov [r] , r
  //   mov r, imm
  //   add, sun
  //   z
  //   c
endmodule

module main (
  input  Cin,
  input  [2:0] in_2,
  input  Sub,
  input  A,
  input  B,
  output Result,
  output Cout
);

  wire adder_1_out, and_1_out, nor_1_out, or_1_out, xor_1_out, xor_2_out;

  xor xor_1 (xor_1_out, B, Sub);
  and and_1 (and_1_out, A, B);
  or or_1 (or_1_out, A, B);
  xor xor_2 (xor_2_out, A, B);
  nor nor_1 (nor_1_out, A, B);
  Adder #(.width(1)) adder_1 (.a(A), .b(xor_1_out), .out(adder_1_out), .cin(Cin), .cout(Cout));
  Multiplexer #(.select(3)) multiplexer_1 (
    .in0(and_1_out), .in1(or_1_out), .in2(xor_2_out), .in3(nor_1_out), .in4(adder_1_out), .in5(adder_1_out),
    .out(Result), .sel(in_2));  // open: in6, in7, en

  // Notes on the sheet:
  //   ALU OPERATIONS ARE
  //   000 AND
  //   001 OR
  //   010 XOR
  //   011 NOR
  //   100 ADD:SUB
  //   FOR SUB SET Sub and Cin pins to 1
endmodule

module ALU4Bit (
  input  [2:0] Op_Select,
  input  [7:0] in_2,
  input  [7:0] in_3,
  output [7:0] \output ,
  output zero_flag,
  output Cout,
  output Sign
);

  wire and_1_out, main_1_cout, main_2_cout, main_3_cout, main_4_cout, main_5_cout, main_6_cout, main_7_cout;

  and and_1 (and_1_out, Op_Select[0], ~Op_Select[1], Op_Select[2]);  // AND_Gate
  main main_1 (
    .A(in_2[0]), .B(in_3[0]), .Result(\output [0]), .in_2(Op_Select), .Cout(main_1_cout), .Cin(and_1_out),
    .Sub(and_1_out));
  main main_2 (
    .A(in_2[1]), .B(in_3[1]), .Result(\output [1]), .in_2(Op_Select), .Cout(main_2_cout), .Cin(main_1_cout),
    .Sub(and_1_out));
  main main_3 (
    .A(in_2[2]), .B(in_3[2]), .Result(\output [2]), .in_2(Op_Select), .Cout(main_3_cout), .Cin(main_2_cout),
    .Sub(and_1_out));
  main main_4 (
    .A(in_2[3]), .B(in_3[3]), .Result(\output [3]), .in_2(Op_Select), .Cout(main_4_cout), .Cin(main_3_cout),
    .Sub(and_1_out));
  main main_5 (
    .A(in_2[4]), .B(in_3[4]), .Result(\output [4]), .in_2(Op_Select), .Cout(main_5_cout), .Cin(main_4_cout),
    .Sub(and_1_out));
  main main_6 (
    .A(in_2[5]), .B(in_3[5]), .Result(\output [5]), .in_2(Op_Select), .Cout(main_6_cout), .Cin(main_5_cout),
    .Sub(and_1_out));
  main main_7 (
    .A(in_2[6]), .B(in_3[6]), .Result(\output [6]), .in_2(Op_Select), .Cout(main_7_cout), .Cin(main_6_cout),
    .Sub(and_1_out));
  main main_8 (
    .A(in_2[7]), .B(in_3[7]), .Result(\output [7]), .in_2(Op_Select), .Cout(Cout), .Cin(main_7_cout),
    .Sub(and_1_out));
  nor nor_1 (zero_flag, \output [0], \output [1], \output [2], \output [3], \output [4], \output [5], \output [6], \output [7]);

  assign Sign = \output [7];
endmodule

module Rightshifter (
  input  [7:0] in_1,
  output [7:0] out_2
);


  assign out_2 = {1'b0, in_1[7:1]};
endmodule

module Leftshifter (
  input  [7:0] in_1,
  output [7:0] out_2,
  output Cout
);


  assign Cout = in_1[7];
  assign out_2 = {in_1[6:0], 1'b0};
endmodule
